// Logisim project TETRIS.circ as structural Verilog: 1 circuit, main circuit main
module main (
  input  in_1,
  input  in_2,
  input  in_3
);

  wire tetris_1_p20, tetris_1_p21, tetris_1_p22;
  wire [6:0] tetris_1_p23;
  wire [7:0] tetris_1_p2, tetris_1_p3, tetris_1_p4, tetris_1_p5, tetris_1_p6, tetris_1_p7, tetris_1_p8,
       tetris_1_p9, tetris_1_p10, tetris_1_p11, tetris_1_p12, tetris_1_p13, tetris_1_p14, tetris_1_p15,
       tetris_1_p16, tetris_1_p17;

  DotMatrix #(.inputtype("row"), .matrixcols(8), .matrixrows(16)) dotmatrix_1 (
    .row0(tetris_1_p2), .row1(tetris_1_p3), .row2(tetris_1_p4), .row3(tetris_1_p5), .row4(tetris_1_p6),
    .row5(tetris_1_p7), .row6(tetris_1_p8), .row7(tetris_1_p9), .row8(tetris_1_p10), .row9(tetris_1_p11),
    .row10(tetris_1_p12), .row11(tetris_1_p13), .row12(tetris_1_p14), .row13(tetris_1_p15),
    .row14(tetris_1_p16), .row15(tetris_1_p17));
  // Tetris tetris_1: pin names not known; wires that end beside it: in_1, tetris_1_p2, tetris_1_p3, tetris_1_p4, tetris_1_p5, tetris_1_p6, tetris_1_p7, tetris_1_p8, tetris_1_p9, tetris_1_p10, tetris_1_p11, tetris_1_p12, tetris_1_p13, tetris_1_p14, tetris_1_p15, tetris_1_p16, tetris_1_p17, in_2, in_3, tetris_1_p20, tetris_1_p21, tetris_1_p22, tetris_1_p23
  Button button_1 (.out(tetris_1_p21));
  Keyboard keyboard_1 (.clr(tetris_1_p20), .avail(tetris_1_p22), .data(tetris_1_p23));  // open: clk, re
endmodule
